# Fritzing sketch Schematic (saved by Fritzing 0.9.3b)
breadboards: 4

parts:
  U1 = ESP8266 NodeMCU LoLin module
  LCM1602_IIC1 = LCM1602 IIC [part_number="LCM1602 IIC" chip_label="LCM1602 IIC" package="DIP (Dual Inline) [THT]"]
  U2 = LCD-16X2 [package=lcd-16x2_noholes]
  LED1 = LED - 5mm [color="Red (633nm)" package="5 mm [THT]"]
  LED2 = LED - 5mm [color="Yellow (595nm)" package="5 mm [THT]"]
  LED3 = LED - 5mm [color="Green (555nm)" package="5 mm [THT]"]
  R1 = Resistor [tolerance=±5% resistance=220 package="0805 [SMD]"]
  R2 = Resistor [tolerance=±5% resistance=220 package="0805 [SMD]"]
  R3 = Resistor [tolerance=±5% resistance=220 package="0805 [SMD]"]
  S1 = Pushbutton [package="[THT]"]
  Part1 = Adafruit TCS34725 RGB Color Sensor [part_number="Adafruit #1334"]
  RE1 = KY-040 Rotary encoder [package=THT]
  U3 = ESP8266 NodeMCU LoLin module
  Part2 = Adafruit TCS34725 RGB Color Sensor [part_number="Adafruit #1334"]
  U4 = ESP8266 NodeMCU LoLin module
  LED4 = LED - 5mm [color="Green (555nm)" package="5 mm [THT]"]
  LED5 = LED - 5mm [color="Yellow (595nm)" package="5 mm [THT]"]
  LED6 = LED - 5mm [color="Red (633nm)" package="5 mm [THT]"]
  R4 = Resistor [tolerance=±5% resistance=220 package="0805 [SMD]"]
  R5 = Resistor [tolerance=±5% resistance=220 package="0805 [SMD]"]
  R6 = Resistor [tolerance=±5% resistance=220 package="0805 [SMD]"]
  U5 = ESP8266 NodeMCU LoLin module
  LED7 = LED - 5mm [color="Green (555nm)" package="5 mm [THT]"]
  LED8 = LED - 5mm [color="Yellow (595nm)" package="5 mm [THT]"]
  LED9 = LED - 5mm [color="Red (633nm)" package="5 mm [THT]"]
  R7 = Resistor [tolerance=±5% resistance=220 package="0805 [SMD]"]
  R8 = Resistor [tolerance=±5% resistance=220 package="0805 [SMD]"]
  R9 = Resistor [tolerance=±5% resistance=220 package="0805 [SMD]"]
  Part4 = Adafruit TCS34725 RGB Color Sensor [part_number="Adafruit #1334"]

nets:
  N1: U1.D1, LCM1602_IIC1.SCL, Part1.SCL
  N2: U1.D2, LCM1602_IIC1.SDA, Part1.SDA
  3V3: U1.3V3, Part1.VIN
  GND: U1.GND, LCM1602_IIC1.GND, LED1.cathode, LED3.cathode, S1.Pin_3, S1.Pin_4, Part1.GND
  N3: U1.D5, S1.Pin_1, S1.Pin_2
  N4: U1.D6, R1.Pin_0
  N5: U1.D7, R2.Pin_0
  N6: U1.D8, R3.Pin_0
  VCC: U1.Vin, LCM1602_IIC1.VCC, RE1.Vcc
  N7: U1.S3, Part1.LED_EN
  VSS: LCM1602_IIC1.VSS, U2.VSS
  VDD: LCM1602_IIC1.VDD, U2.VDD
  N8: LCM1602_IIC1.V0, U2.VO
  N9: LCM1602_IIC1.RS, U2.RS
  N10: LCM1602_IIC1.RW, U2.R_W
  N11: LCM1602_IIC1.E, U2.E
  N12: LCM1602_IIC1.D0, U2.DB0
  N13: LCM1602_IIC1.D1, U2.DB1
  N14: LCM1602_IIC1.D2, U2.DB2
  N15: LCM1602_IIC1.D3, U2.DB3
  N16: LCM1602_IIC1.D4, U2.DB4
  N17: LCM1602_IIC1.D5, U2.DB5
  N18: LCM1602_IIC1.D6, U2.DB6
  N19: LCM1602_IIC1.D7, U2.DB7
  N20: LCM1602_IIC1.A, U2.A
  N21: LCM1602_IIC1.K, U2.K
  N22: LED1.anode, R1.Pin_1
  N23: LED2.anode, R2.Pin_1
  N24: LED3.anode, R3.Pin_1
  N25: U3.D1, Part2.SCL
  N26: U3.D2, Part2.SDA
  3V3_2: U3.3V3, Part2.VIN
  GND_2: U3.GND, Part2.GND
  N27: U3.S3, Part2.LED_EN
  N28: U4.GND, LED4.cathode, LED6.cathode
  N29: U4.D6, R6.Pin_0
  N30: U4.D7, R5.Pin_0
  N31: U4.D8, R4.Pin_0
  N32: LED4.anode, R4.Pin_1
  N33: LED5.anode, R5.Pin_1
  N34: LED6.anode, R6.Pin_1
  N35: U5.D1, Part4.SCL
  N36: U5.D2, Part4.SDA
  3V3_3: U5.3V3, Part4.VIN
  GND_3: U5.GND, LED7.cathode, LED9.cathode, Part4.GND
  N37: U5.D6, R9.Pin_0
  N38: U5.D7, R8.Pin_0
  N39: U5.D8, R7.Pin_0
  N40: U5.S3, Part4.LED_EN
  N41: LED7.anode, R7.Pin_1
  N42: LED8.anode, R8.Pin_1
  N43: LED9.anode, R9.Pin_1

custom parts:
  ESP8266 NodeMCU LoLin module: ESP8266 based NodeMCU
  LCM1602 IIC: I2C-Module to use a 1602 or 2004 LCD on with the wire.h libory Serial LCD Modul
  Adafruit TCS34725 RGB Color Sensor: Your electronics can now see in dazzling color with this lovely color light sensor. We found the best color sensor on the market, the TCS34725, which has RGB and Clear light sensing elements. An IR blocking filter, integrated on-chip and localized to the color sensing photodiodes, minimizes the IR spectral component of the incoming light and allows color measurements to be made accurately. The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
  KY-040 Rotary encoder: KY-040 Rotary Encoder with switch on breakout borad from AZ Delivery
